# Fritzing sketch diagram (saved by Fritzing 0.9.3b)

parts:
  Part1 = Arduino Uno (Rev3) - ICSP
  e-radionica_com1 = LM393 LDR breakout [part_number=100027]
  LCD2 = LCD screen
  LCM1602_IIC2 = LCM1602 IIC [part_number="LCM1602 IIC" chip_label="LCM1602 IIC" package="DIP (Dual Inline) [THT]"]
  SPKR1 = Loudspeaker
  S1 = Pushbutton [package="[THT]"]
  S2 = Pushbutton [package="[THT]"]
  S3 = Pushbutton [package="[THT]"]
  S4 = Pushbutton [package="[THT]"]

nets:
  N1: Part1.A4/SDA, LCM1602_IIC2.SDA
  N2: Part1.A5/SCL, LCM1602_IIC2.SCL
  N3: Part1.D2, e-radionica_com1.DO
  N4: Part1.D3_PWM, SPKR1.pin2
  N5: Part1.D4, S4.Pin_2
  N6: Part1.D5_PWM, S3.Pin_2
  N7: Part1.D6_PWM, S2.Pin_2
  N8: Part1.D7, S1.Pin_2
  5V: Part1.5V, e-radionica_com1.VCC
  GND: Part1.GND, e-radionica_com1.GND
  VSS: LCD2.VSS, LCM1602_IIC2.VSS
  VDD: LCD2.VDD, LCM1602_IIC2.VDD
  N9: LCD2.V0, LCM1602_IIC2.V0
  N10: LCD2.RS, LCM1602_IIC2.RS
  N11: LCD2.R/W, LCM1602_IIC2.RW
  N12: LCD2.E, LCM1602_IIC2.E
  N13: LCD2.DB0, LCM1602_IIC2.D0
  N14: LCD2.DB1, LCM1602_IIC2.D1
  N15: LCD2.DB2, LCM1602_IIC2.D2
  N16: LCD2.DB3, LCM1602_IIC2.D3
  N17: LCD2.DB4, LCM1602_IIC2.D4
  N18: LCD2.DB5, LCM1602_IIC2.D5
  N19: LCD2.DB6, LCM1602_IIC2.D6
  N20: LCD2.DB7, LCM1602_IIC2.D7
  N21: LCD2.LED+, LCM1602_IIC2.A
  N22: LCD2.LED-, LCM1602_IIC2.K
  N23: LCM1602_IIC2.GND, SPKR1.pin1
  N24: LCM1602_IIC2.LED_A, LCM1602_IIC2.LED_B
  N25: S1.Pin_4, S2.Pin_3, S2.Pin_4

notes:
  Buzzer
  Arduino Uno Development Board
  16*2 LCD Module and I2c Interface Board
  LDR Module
  KwH Alarm set Button
  Up Button
  Down Button
  Manual Kwh send Button

custom parts:
  LCM1602 IIC: I2C-Module to use a 1602 or 2004 LCD on with the wire.h libory Serial LCD Modul
